# Fritzing sketch skeleton_layout (saved by Fritzing 0.9.4)
breadboards: 1

parts:
  SW3 = DIP Switch 8 Position [package=dipswitch-08]
  Basic_IO_Shield1 = chipKIT Basic I/O Shield [chip_label=IC package="DIP (Dual Inline) [THT]"]

nets:
  N1: SW3.1, SW3.2, SW3.3, SW3.4, SW3.5, SW3.6, Basic_IO_Shield1.GND, Basic_IO_Shield1.D28, Basic_IO_Shield1.D29, Basic_IO_Shield1.D30, Basic_IO_Shield1.D31, Basic_IO_Shield1.D32, Basic_IO_Shield1.D33
  N2: SW3.11, SW3.12, SW3.13, SW3.14, SW3.15, SW3.16, Basic_IO_Shield1.3V3

custom parts:
  chipKIT Basic I/O Shield: The chipKIT Basic I/O Shield is an input/output expansion board designed for use with chipKIT microcontroller boards such as the Uno32™ and the Max32™. The Basic I/O Shield is designed to provide a range of input/output devices suitable for beginners learning about microcontrollers and various types of I/O devices, or for use by more advanced user to provide inputs or outputs for their own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
